// Logisim project Sweet16MCU.circ as structural Verilog: 1 circuit, main circuit main
module main (
  input  [15:0] IRQ,
  input  [15:0] Reset,
  input  RST,
  input  [15:0] in_4
);

  wire comparator_1_eq, comparator_2_lt, comparator_3_eq, D_OUT_WE, demultiplexer_3_out1,
       demultiplexer_3_out2, demultiplexer_3_out3, demultiplexer_3_out4, demultiplexer_3_out5,
       demultiplexer_3_out6, demultiplexer_3_out7, IR_WE, MST_CLK, not_2_out, or_1_out, PC_WE, R7_LD, RAM_WE,
       REG_WE, SEL_WB, xor_1_out;
  wire [1:0] IR_q_2, SEL_PC;
  wire [2:0] SA, SB, SD, uPC_q, uPC_WB;
  wire [4:0] SI;
  wire [5:0] DISP_SEG;
  wire [7:3] uROM_data;
  wire [9:0] demultiplexer_1_out0, demultiplexer_1_out1, demultiplexer_1_out2, demultiplexer_1_out3,
       demultiplexer_1_out4, demultiplexer_1_out5, demultiplexer_1_out6, demultiplexer_1_out7,
       demultiplexer_1_out8, demultiplexer_1_out9, demultiplexer_1_out10, demultiplexer_1_out11,
       demultiplexer_1_out12, demultiplexer_1_out13, demultiplexer_1_out14, demultiplexer_1_out15,
       demultiplexer_1_out16, demultiplexer_1_out17, demultiplexer_1_out18, demultiplexer_1_out19,
       demultiplexer_1_out20, demultiplexer_1_out21, demultiplexer_1_out22, demultiplexer_1_out23,
       demultiplexer_1_out24, demultiplexer_1_out25, demultiplexer_1_out26, demultiplexer_1_out27,
       demultiplexer_1_out28, demultiplexer_1_out29, demultiplexer_1_out30, demultiplexer_1_out31,
       demultiplexer_1_out32, demultiplexer_1_out33, demultiplexer_1_out34, demultiplexer_1_out35,
       demultiplexer_1_out36, demultiplexer_1_out37, demultiplexer_1_out38, demultiplexer_1_out39,
       demultiplexer_1_out40, demultiplexer_1_out41, demultiplexer_1_out42, demultiplexer_1_out43,
       demultiplexer_1_out44, demultiplexer_1_out45, demultiplexer_1_out46, demultiplexer_1_out47,
       demultiplexer_1_out48, demultiplexer_1_out49, demultiplexer_1_out50, demultiplexer_1_out51,
       demultiplexer_1_out52, demultiplexer_1_out53, demultiplexer_1_out54, demultiplexer_1_out55,
       demultiplexer_1_out56, demultiplexer_1_out57, demultiplexer_1_out58, demultiplexer_1_out59,
       demultiplexer_1_out60, demultiplexer_1_out61, demultiplexer_1_out62, demultiplexer_1_out63, DISP_D;
  wire [13:0] IR_q;
  wire [15:0] adder_1_out, adder_2_out, adder_3_out, adder_4_out, and_1_out, BIG_IMM, bit_extender_1_out,
       bit_extender_2_out, D_OUT, EX_D_IN, JMP, multiplexer_1_out, multiplexer_2_out, multiplexer_3_out,
       multiplexer_6_out, or_2_out, PC, PROGMEM_data, Reg1_q, Reg2_q, Reg3_q, Reg4_q, Reg5_q, Reg6_q, Reg7_q,
       SA_D, SB_D, shifter_1_out, shifter_2_out, subtractor_1_out, xor_2_out;
  wire [15:14] demultiplexer_2_out1;

  DotMatrix #(.dotshape("circle"), .matrixcols(64), .matrixrows(10), .persist(2048)) Display (
    .col0(demultiplexer_1_out0), .col1(demultiplexer_1_out1), .col2(demultiplexer_1_out2),
    .col3(demultiplexer_1_out3), .col4(demultiplexer_1_out4), .col5(demultiplexer_1_out5),
    .col6(demultiplexer_1_out6), .col7(demultiplexer_1_out7), .col8(demultiplexer_1_out8),
    .col9(demultiplexer_1_out9), .col10(demultiplexer_1_out10), .col11(demultiplexer_1_out11),
    .col12(demultiplexer_1_out12), .col13(demultiplexer_1_out13), .col14(demultiplexer_1_out14),
    .col15(demultiplexer_1_out15), .col16(demultiplexer_1_out16), .col17(demultiplexer_1_out17),
    .col18(demultiplexer_1_out18), .col19(demultiplexer_1_out19), .col20(demultiplexer_1_out20),
    .col21(demultiplexer_1_out21), .col22(demultiplexer_1_out22), .col23(demultiplexer_1_out23),
    .col24(demultiplexer_1_out24), .col25(demultiplexer_1_out25), .col26(demultiplexer_1_out26),
    .col27(demultiplexer_1_out27), .col28(demultiplexer_1_out28), .col29(demultiplexer_1_out29),
    .col30(demultiplexer_1_out30), .col31(demultiplexer_1_out31), .col32(demultiplexer_1_out32),
    .col33(demultiplexer_1_out33), .col34(demultiplexer_1_out34), .col35(demultiplexer_1_out35),
    .col36(demultiplexer_1_out36), .col37(demultiplexer_1_out37), .col38(demultiplexer_1_out38),
    .col39(demultiplexer_1_out39), .col40(demultiplexer_1_out40), .col41(demultiplexer_1_out41),
    .col42(demultiplexer_1_out42), .col43(demultiplexer_1_out43), .col44(demultiplexer_1_out44),
    .col45(demultiplexer_1_out45), .col46(demultiplexer_1_out46), .col47(demultiplexer_1_out47),
    .col48(demultiplexer_1_out48), .col49(demultiplexer_1_out49), .col50(demultiplexer_1_out50),
    .col51(demultiplexer_1_out51), .col52(demultiplexer_1_out52), .col53(demultiplexer_1_out53),
    .col54(demultiplexer_1_out54), .col55(demultiplexer_1_out55), .col56(demultiplexer_1_out56),
    .col57(demultiplexer_1_out57), .col58(demultiplexer_1_out58), .col59(demultiplexer_1_out59),
    .col60(demultiplexer_1_out60), .col61(demultiplexer_1_out61), .col62(demultiplexer_1_out62),
    .col63(demultiplexer_1_out63));
  // Probe on IR_WE
  // Probe on SEL_WB
  // Probe on REG_WE
  // Probe on PC_WE
  // Probe on SEL_PC
  // Probe on D_OUT_WE
  // Probe on RAM_WE
  Register #(.width(16)) DISP_CTL (.D(D_OUT), .en(D_OUT_WE), .clk(MST_CLK), .Q({DISP_D, DISP_SEG}), .clr(RST));
  // Probe on SI
  // Probe on SD
  // Probe on SA
  // Probe on SB
  Clock CLK (.out(MST_CLK));
  Demultiplexer #(.select(6), .width(10)) demultiplexer_1 (
    .out0(demultiplexer_1_out0), .out1(demultiplexer_1_out1), .out2(demultiplexer_1_out2),
    .out3(demultiplexer_1_out3), .out4(demultiplexer_1_out4), .out5(demultiplexer_1_out5),
    .out6(demultiplexer_1_out6), .out7(demultiplexer_1_out7), .out8(demultiplexer_1_out8),
    .out9(demultiplexer_1_out9), .out10(demultiplexer_1_out10), .out11(demultiplexer_1_out11),
    .out12(demultiplexer_1_out12), .out13(demultiplexer_1_out13), .out14(demultiplexer_1_out14),
    .out15(demultiplexer_1_out15), .out16(demultiplexer_1_out16), .out17(demultiplexer_1_out17),
    .out18(demultiplexer_1_out18), .out19(demultiplexer_1_out19), .out20(demultiplexer_1_out20),
    .out21(demultiplexer_1_out21), .out22(demultiplexer_1_out22), .out23(demultiplexer_1_out23),
    .out24(demultiplexer_1_out24), .out25(demultiplexer_1_out25), .out26(demultiplexer_1_out26),
    .out27(demultiplexer_1_out27), .out28(demultiplexer_1_out28), .out29(demultiplexer_1_out29),
    .out30(demultiplexer_1_out30), .out31(demultiplexer_1_out31), .out32(demultiplexer_1_out32),
    .out33(demultiplexer_1_out33), .out34(demultiplexer_1_out34), .out35(demultiplexer_1_out35),
    .out36(demultiplexer_1_out36), .out37(demultiplexer_1_out37), .out38(demultiplexer_1_out38),
    .out39(demultiplexer_1_out39), .out40(demultiplexer_1_out40), .out41(demultiplexer_1_out41),
    .out42(demultiplexer_1_out42), .out43(demultiplexer_1_out43), .out44(demultiplexer_1_out44),
    .out45(demultiplexer_1_out45), .out46(demultiplexer_1_out46), .out47(demultiplexer_1_out47),
    .out48(demultiplexer_1_out48), .out49(demultiplexer_1_out49), .out50(demultiplexer_1_out50),
    .out51(demultiplexer_1_out51), .out52(demultiplexer_1_out52), .out53(demultiplexer_1_out53),
    .out54(demultiplexer_1_out54), .out55(demultiplexer_1_out55), .out56(demultiplexer_1_out56),
    .out57(demultiplexer_1_out57), .out58(demultiplexer_1_out58), .out59(demultiplexer_1_out59),
    .out60(demultiplexer_1_out60), .out61(demultiplexer_1_out61), .out62(demultiplexer_1_out62),
    .out63(demultiplexer_1_out63), .in(DISP_D), .sel(DISP_SEG));
  Adder #(.width(16)) adder_1 (.a(PC), .b(16'h1), .out(adder_1_out), .cin(1'b0));  // open: cout
  Multiplexer #(.select(2), .width(16)) multiplexer_1 (
    .in0(adder_1_out), .in1(JMP), .in2(IRQ), .in3(Reset), .out(multiplexer_1_out), .sel(SEL_PC));
  Register #(.width(16)) u_PC (.D(multiplexer_1_out), .en(PC_WE), .clk(MST_CLK), .Q(PC), .clr(RST));
  Register #(.width(3)) uPC (.D(uPC_WB), .en(1'b1), .clk(MST_CLK), .Q(uPC_q), .clr(RST));
  // Probe on uPC_q
  ROM #(.addrWidth(16), .dataWidth(16)) PROGMEM (.addr(PC), .data(PROGMEM_data));
  ROM #(.dataWidth(16)) uROM (
    .addr({SI, uPC_q}),
    .data({IR_WE, SEL_WB, REG_WE, PC_WE, SEL_PC[0], SEL_PC[1], D_OUT_WE, RAM_WE, uROM_data, uPC_WB}));
  RAM #(.addrWidth(16), .dataWidth(16)) VOLMEM (
    .addr(SA_D), .we(RAM_WE), .oe(1'b1), .clk(MST_CLK), .din(D_OUT), .dout(EX_D_IN));
  Register #(.width(16)) IR (.D(PROGMEM_data), .en(IR_WE), .clk(MST_CLK), .Q({IR_q_2, IR_q}), .clr(RST));
  xor xor_1 (xor_1_out, IR_q_2[1], IR_q_2[0]);
  not not_1 (R7_LD, xor_1_out);
  Demultiplexer #(.width(16)) demultiplexer_2 (
    .out0(BIG_IMM), .out1({demultiplexer_2_out1, SI, SD, SA, SB}), .in({IR_q_2, IR_q}), .sel(xor_1_out));
  Pull_Resistor pull_resistor_1 (.node({demultiplexer_2_out1, SI, SD, SA, SB}));
  Demultiplexer #(.select(3)) demultiplexer_3 (
    .out1(demultiplexer_3_out1), .out2(demultiplexer_3_out2), .out3(demultiplexer_3_out3),
    .out4(demultiplexer_3_out4), .out5(demultiplexer_3_out5), .out6(demultiplexer_3_out6),
    .out7(demultiplexer_3_out7), .in(REG_WE), .sel(SD));  // open: out0
  Multiplexer #(.width(16)) multiplexer_2 (.in0(D_OUT), .in1(EX_D_IN), .out(multiplexer_2_out), .sel(SEL_WB));
  or or_1 (or_1_out, demultiplexer_3_out7, R7_LD);
  Register #(.width(16)) Reg1 (.D(multiplexer_2_out), .en(demultiplexer_3_out1), .clk(MST_CLK), .Q(Reg1_q), .clr(RST));
  Register #(.width(16)) Reg2 (.D(multiplexer_2_out), .en(demultiplexer_3_out2), .clk(MST_CLK), .Q(Reg2_q), .clr(RST));
  Register #(.width(16)) Reg3 (.D(multiplexer_2_out), .en(demultiplexer_3_out3), .clk(MST_CLK), .Q(Reg3_q), .clr(RST));
  Register #(.width(16)) Reg4 (.D(multiplexer_2_out), .en(demultiplexer_3_out4), .clk(MST_CLK), .Q(Reg4_q), .clr(RST));
  Register #(.width(16)) Reg5 (.D(multiplexer_2_out), .en(demultiplexer_3_out5), .clk(MST_CLK), .Q(Reg5_q), .clr(RST));
  Register #(.width(16)) Reg6 (.D(multiplexer_2_out), .en(demultiplexer_3_out6), .clk(MST_CLK), .Q(Reg6_q), .clr(RST));
  Register #(.width(16)) Reg7 (.D(multiplexer_3_out), .en(or_1_out), .clk(MST_CLK), .Q(Reg7_q), .clr(RST));
  Multiplexer #(.width(16)) multiplexer_3 (
    .in0(multiplexer_2_out), .in1(BIG_IMM), .out(multiplexer_3_out), .sel(R7_LD));
  Multiplexer #(.select(3), .width(16)) multiplexer_4 (
    .in0({16{1'b0}}), .in1(Reg1_q), .in2(Reg2_q), .in3(Reg3_q), .in4(Reg4_q), .in5(Reg5_q), .in6(Reg6_q),
    .in7(Reg7_q), .out(SA_D), .sel(SA));
  Multiplexer #(.select(3), .width(16)) multiplexer_5 (
    .in0({16{1'b0}}), .in1(Reg1_q), .in2(Reg2_q), .in3(Reg3_q), .in4(Reg4_q), .in5(Reg5_q), .in6(Reg6_q),
    .in7(Reg7_q), .out(SB_D), .sel(SB));
  Comparator #(.mode("unsigned"), .width(16)) comparator_1 (
    .a(SA_D), .b({16{1'b0}}), .eq(comparator_1_eq));  // open: gt, lt
  Adder #(.width(16)) adder_2 (.a(SB_D), .b(PC), .out(adder_2_out), .cin(1'b0));  // open: cout
  Adder #(.width(16)) adder_3 (.a(PC), .b(16'h1), .out(adder_3_out), .cin(1'b0));  // open: cout
  Comparator #(.mode("unsigned"), .width(16)) comparator_2 (.a(SA_D), .b(SB_D), .lt(comparator_2_lt));  // open: gt, eq
  assign bit_extender_1_out = {{15{1'b0}}, comparator_2_lt};  // Bit_Extender bit_extender_1
  Adder #(.width(16)) adder_4 (.a(SA_D), .b(SB_D), .out(adder_4_out), .cin(1'b0));  // open: cout
  Subtractor #(.width(16)) subtractor_1 (.a(SA_D), .b(SB_D), .out(subtractor_1_out), .bin(1'b0));  // open: bout
  assign and_1_out = SA_D & SB_D;  // AND_Gate and_1, 16 bits wide
  assign or_2_out = SA_D | SB_D;  // OR_Gate or_2, 16 bits wide
  assign xor_2_out = SA_D ^ SB_D;  // XOR_Gate xor_2, 16 bits wide
  Shifter #(.width(16)) shifter_1 (.in(SA_D), .\dist (4'b0001), .out(shifter_1_out));
  Shifter #(.shift("lr"), .width(16)) shifter_2 (.in(SA_D), .\dist (4'b0001), .out(shifter_2_out));
  assign bit_extender_2_out = {{10{SA[2]}}, {SA, SB}};  // Bit_Extender bit_extender_2
  not not_2 (not_2_out, comparator_1_eq);
  Multiplexer #(.width(16)) multiplexer_6 (
    .in0(adder_2_out), .in1(adder_3_out), .out(multiplexer_6_out), .sel(not_2_out));
  Multiplexer #(.width(16)) multiplexer_7 (.in0(multiplexer_6_out), .in1(SA_D), .out(JMP), .sel(comparator_3_eq));
  Comparator #(.mode("unsigned"), .width(5)) comparator_3 (.a(5'b01011), .b(SI), .eq(comparator_3_eq));  // open: gt, lt
  // Probe on D_OUT
  Multiplexer #(.select(5), .width(16)) multiplexer_8 (
    .in0(bit_extender_1_out), .in1(adder_4_out), .in2(subtractor_1_out), .in3(and_1_out), .in4(or_2_out),
    .in5(xor_2_out), .in6(shifter_1_out), .in7(shifter_2_out), .in8(in_4), .in9(bit_extender_2_out),
    .in10(adder_3_out), .in11(SA_D), .in12(SB_D), .in13(SB_D), .in14(SB_D), .in15({16{1'b0}}),
    .in16({16{1'b0}}), .in17({16{1'b0}}), .in18({16{1'b0}}), .in19({16{1'b0}}), .in20({16{1'b0}}),
    .in21({16{1'b0}}), .in22({16{1'b0}}), .in23({16{1'b0}}), .in24({16{1'b0}}), .in25({16{1'b0}}),
    .in26({16{1'b0}}), .in27({16{1'b0}}), .in28({16{1'b0}}), .in29({16{1'b0}}), .in30({16{1'b0}}),
    .in31({16{1'b0}}), .out(D_OUT), .sel(SI));

  // Other names for the same wires on the sheet: IN_D_IN[15:0] = in_4

  // Notes on the sheet:
  //   External I/O
  //   Display Controller
  //   Display
  //   BIT0-2:SB
  //   BIT3-5:SA
  //   BIT6-8:SD
  //   BIT9-13:SI
  //   BIT14-15:NC
  //   contents of PROGMEM (hex, n*v repeats v):
  //   33 5638 5340 5382 3f 4278 52c3 53fa 430d 5b20 4921 5804 540b 444a 5407 3f 4278 45b2 5b00 4200 5800
  //   530a 5434 7*4200 530d 5404 5382 436a c0 44ef 5304 541c 4200 5304 5404 5340 5301 5404 5*4200 6 5638
  //   5281 bf 4278 5383 52fd 5c08 540e 444a 5403 3f80 4df8 5c0f 424a 3fc0 4df8 5c0f 424a 300 5c0f 424a 600
  //   5c0f 424a f00 5c0f 424a 600 5c0f 424a 300 5c0f 424a 3fc0 4df8 5c0f 424a 3f80 4df8 5c0f 5302 424c 700
  //   5c0f 424a f80 5c0f 424a a80 5c0f 424a e80 5c0f 424a 680 5c0f 5304 424c 1f80 5c0f 424a 3f80 5c0f 424a
  //   3300 4df8 5c0f 424a 2300 4df8 5c0f 424a 3300 4df8 5c0f 424a 3f80 5c0f 424a 1f80 5c0f 5302 424c f80
  //   5c0f 424a f80 5c0f 424a 400 5c0f 424a c00 5c0f 5302 424c 700 5c0f 424a f80 5c0f 424a a80 5c0f 424a
  //   e80 5c0f 424a 680 5c0f 5304 424c 3fc0 4df8 5c0f 424a 3fc0 4df8 5c0f 424a 3000 5c0f 424a 1800 5c0f
  //   424a c00 5c0f 424a 1800 5c0f 424a 3000 5c0f 424a 3fc0 4df8 5c0f 424a 3fc0 4df8 5c0f 5302 424c 900
  //   5c0f 424a b80 5c0f 424a a80 5c0f 424a f80 5c0f 424a 780 5c0f 5302 424c f80 5c0f 424a f80 5c0f 424a
  //   400 5c0f 424a c00 5c0f 5302 424c 480 5c0f 424a e80 5c0f 424a a80 5c0f 424a b80 5c0f 424a 900 5c0f
  //   5302 424c 3fc0 4df8 5c0f 424a 3fc0 4df8 5c0f 424a 800 5c0f 424a f80 5c0f 424a 780 5c0f 5302 424c 900
  //   5c0f 424a b80 5c0f 424a a80 5c0f 424a f80 5c0f 424a 780 5c0f 5302 424c 3fc0 4df8 5c0f 424a 3fc0 4df8
  //   5c0f 5302 424c 3fc0 4df8 5c0f 424a 3fc0 4df8 5c0f 5304 424c 600 5c0f 424a 600 5c0f 424a 600 5c0f
  //   424a 600 5c0f 5304 424c 3fc0 4df8 5c0f 424a 3fc0 4df8 5c0f 424a 36c0 4df8 5c0f 424a 36c0 4df8 5c0f
  //   424a 36c0 4df8 5c0f 424a 36c0 4df8 5c0f 424a 30c0 4df8 5c0f 5302 424c 3fc0 4df8 5c0f 424a 3fc0 4df8
  //   5c0f 424a 36c0 4df8 5c0f 424a 36c0 4df8 5c0f 424a 36c0 4df8 5c0f 424a 36c0 4df8 5c0f 424a 30c0 4df8
  //   5c0f 5302 424c 2100 5c0f 424a 30c0 4df8 5c0f 424a 2440 4df8 5c0f 424a 2440 4df8 5c0f 424a 2440 4df8
  //   5c0f 424a 3fc0 4df8 5c0f 424a 3700 5c0f 5302 424c 600 5c0f 424a e00 5c0f 424a 1a00 5c0f 424a 3200
  //   5c0f 424a 3fc0 4df8 5c0f 424a 3fc0 4df8 5c0f 424a 200 5c0f 5302 424c 3f00 5c0f 424a 3fc0 4df8 5c0f
  //   424a 2040 4df8 5c0f 424a 2040 4df8 5c0f 424a 2040 4df8 5c0f 424a 3fc0 4df8 5c0f 424a 3f00 5c0f c0
  //   42f8 3f 4278 5383 53fb 5b08 434b 5c2c 540e 444a 5407 2 5638
  //   contents of uROM (hex, n*v repeats v):
  //   8001 3000 6*0 8001 3000 6*0 8001 3000 6*0 8001 3000 6*0 8001 3000 6*0 8001 3000 6*0 8001 3000 6*0
  //   8001 3000 6*0 8001 3000 6*0 8001 3000 6*0 8001 3800 6*0 8001 1800 6*0 8001 1200 6*0 8001 2 7000 5*0
  //   8001 1100 6*0 8001 7*0 8001 7*0 8001 7*0 8001 7*0 8001 7*0 8001 7*0 8001 7*0 8001 7*0 8001 7*0 8001
  //   7*0 8001 7*0 8001 7*0 8001 7*0 8001 7*0 8001 7*0 8001 7*0 8001 1c00
  //   Control Unit
  //   uControl Unit
  //   Storage
  //   Reg_Stack
  //   "Reg0"
  //   Reg_Select
  //   ALU
  //   Op_Select
endmodule
